// Logisim project 8BitALU.circ as structural Verilog: 2 circuits, main circuit ALU
module ALU (
  input  [7:0] A,
  input  [7:0] B,
  input  [3:0] Op,
  output Carry,
  output [7:0] Y,
  output Gt,
  output Eq,
  output Lt
);

  wire comparator_1_eq, comparator_1_gt, comparator_1_lt, comparator_2_eq;
  wire [7:0] adder_1_out, adder_2_out, adder_3_out, and_1_out, not_1_out, or_1_out, shifter_1_out,
       shifter_2_out;

  Adder adder_1 (.a(A), .b(B), .out(adder_1_out), .cin(1'b0), .cout(Carry));
  Adder adder_2 (.a(A), .b(8'h1), .out(adder_2_out));  // open: cin, cout
  Adder adder_3 (.a({8{1'b1}}), .b(A), .out(adder_3_out));  // open: cin, cout
  assign not_1_out = ~A;  // NOT_Gate not_1, 8 bits wide
  assign and_1_out = A & B;  // AND_Gate and_1, 8 bits wide
  assign or_1_out = B | A;  // OR_Gate or_1, 8 bits wide
  Shifter #(.shift("lr")) shifter_1 (.in(A), .\dist (3'b001), .out(shifter_1_out));
  Shifter shifter_2 (.in(A), .\dist (3'b001), .out(shifter_2_out));
  Comparator comparator_1 (.a(A), .b(B), .gt(comparator_1_gt), .eq(comparator_1_eq), .lt(comparator_1_lt));
  and and_2 (Gt, comparator_1_gt, comparator_2_eq);
  and and_3 (Eq, comparator_1_eq, comparator_2_eq);
  and and_4 (Lt, comparator_1_lt, comparator_2_eq);
  Multiplexer #(.select(4), .width(8), .disabled(0), .enable("false")) multiplexer_1 (
    .in0(adder_1_out), .in1(adder_2_out), .in2(adder_3_out), .in3(not_1_out), .in4(and_1_out),
    .in5(or_1_out), .in6(shifter_1_out), .in7(shifter_2_out), .out(Y), .sel(Op));  // open: in8, in9, in10, in11, in12, in13, in14, in15
  Comparator #(.width(4)) comparator_2 (.a(Op), .b(4'b1000), .eq(comparator_2_eq));  // open: gt, lt

  // Notes on the sheet:
  //   Adder
endmodule

module CU (
  input  [7:0] Data_In,
  input  Enable_Write_A,
  input  Data_In___Result,
  input  [7:0] Data_In_2,
  input  [3:0] Op_Code,
  output [7:0] Y,
  output GT,
  output EQ,
  output LT
);

  wire clock_1_out;
  wire [7:0] multiplexer_1_out, Register_A_q, Register_B_q;

  Multiplexer #(.width(8), .disabled(0), .enable("false")) multiplexer_1 (
    .in0(Data_In), .in1(Y), .out(multiplexer_1_out), .sel(Data_In___Result));
  Clock clock_1 (.out(clock_1_out));
  Register Register_A (.D(multiplexer_1_out), .en(Enable_Write_A), .Q(Register_A_q), .clk(clock_1_out));  // open: clr
  Register Register_B (.D(Data_In_2), .en(1'b1), .Q(Register_B_q), .clk(clock_1_out));  // open: clr
  ALU ALU (.A(Register_A_q), .B(Register_B_q), .Op(Op_Code), .Y(Y), .Gt(GT), .Eq(EQ), .Lt(LT));  // open: Carry

  // Notes on the sheet:
  //   0000: Add (A + B)
  //   0001: Increment (A)
  //   0011: NOT (A)
  //   0100: AND (A && B)
  //   Op Codes:
  //   0010: Decrement (A)
  //   0101: OR (A ||  B)
  //   0110: Right Logic Shift (A)
  //   0111: Left Logic Shift (A)
  //   1000: Compare (A&B)
endmodule
